// Logisim project COUNTER.circ as structural Verilog: 1 circuit, main circuit main
module main (
  input  in_1,
  input  in_2,
  input  in_3,
  input  [3:0] in_4,
  input  in_5
);

  wire clock_1_out;
  wire [2:2] comparator_1_gt;
  wire [3:0] adder_1_out, counter_1_q;
  wire [3:3] adder_1_cout;
  wire [6:0] rom_1_data, rom_2_data;

  Counter #(.max('hf), .width(4)) counter_1 (
    .clr(in_1), .load(in_1), .up(in_2), .clk(clock_1_out), .Q(counter_1_q));  // open: count, D, carry
  Clock clock_1 (.out(clock_1_out));
  Comparator #(.mode("unsigned"), .width(4)) comparator_1 (
    .a(counter_1_q), .b(in_4), .gt(comparator_1_gt[2]));  // open: eq, lt
  ROM #(.addrWidth(4), .dataWidth(7)) rom_1 (.addr(adder_1_out), .data(rom_1_data));
  Adder #(.width(4)) adder_1 (
    .a(counter_1_q), .b({in_3, {2{comparator_1_gt[2]}}, in_3}), .out(adder_1_out), .cin(in_3),
    .cout(adder_1_cout[3]));
  ROM #(.addrWidth(4), .dataWidth(7)) rom_2 (.addr({adder_1_cout[3], {3{in_5}}}), .data(rom_2_data));
  _7_Segment_Display u_7_segment_display_1 (
    .g(rom_2_data[0]), .f(rom_2_data[1]), .a(rom_2_data[6]), .b(rom_2_data[5]), .e(rom_2_data[2]),
    .d(rom_2_data[3]), .c(rom_2_data[4]));  // open: dp
  _7_Segment_Display u_7_segment_display_2 (
    .g(rom_1_data[0]), .f(rom_1_data[1]), .a(rom_1_data[6]), .b(rom_1_data[5]), .e(rom_1_data[2]),
    .d(rom_1_data[3]), .c(rom_1_data[4]));  // open: dp

  // Notes on the sheet:
  //   contents of rom_1 (hex, n*v repeats v):
  //   7e 30 6d 79 33 5b 5f 70 7f 7b
  //   contents of rom_2 (hex, n*v repeats v):
  //   8*0 30
endmodule
